// Digital circuit ALU8bits.dig as structural Verilog
module ALU8bits (
  input  [7:0] N,
  input  [2:0] S,
  input  CLK,
  output [7:0] MQ,
  output neg,
  output [7:0] AC,
  output Over
);

  wire neg_t, Over_t, sMQ;
  wire [7:0] _000, _001, _010, _011, _100, _101, _110, _111, MQ0, MQ1, multiplexer_1_out, multiplexer_2_out;

  and and_1 (sMQ, S[0], S[1], ~S[2]);  // And
  soma8bits _000___Soma (.A(AC), .B(N), .S(_000), .Over(Over_t));
  sub8bits \_001___Subtração  (.A(AC), .B(N), .Sub(_001), .neg(neg_t));
  multiplicacao8bits \_010___Multiplicação  (.A(AC), .B(N), .LSB(_010), .MSB(MQ0));
  divisor8bits \_011___Divisão  (.A(AC), .B(N), .R(_011), .Q(MQ1));
  LeftShift8bits _100___Left_Shift (.A(AC), .ALS(_100));
  RightShift8bits _101___Right_Shift (.A(AC), .ARS(_101));
  nand8bits _110___NAND (.A(AC), .B(N), .A_B(_110));
  XOR8bits _111___XOR (.A(AC), .B(N), .A_B(_111));
  Multiplexer #(.Bits(8)) multiplexer_1 (.sel(sMQ), .in_0(MQ0), .in_1(MQ1), .out(multiplexer_1_out));
  Multiplexer #(.Bits(8), .Selector_Bits(3)) multiplexer_2 (
    .sel(S), .in_0(_000), .in_1(_001), .in_2(_010), .in_3(_011), .in_4(_100), .in_5(_101), .in_6(_110),
    .in_7(_111), .out(multiplexer_2_out));
  Register #(.Bits(8)) u_MQ (.D(multiplexer_1_out), .C(CLK), .en(1'b1), .Q(MQ));
  Register #(.Bits(8)) u_AC (.D(multiplexer_2_out), .C(CLK), .en(1'b1), .Q(AC));
  and and_2 (Over, Over_t, ~S[0], ~S[1], ~S[2]);  // And
  and and_3 (neg, neg_t, S[0], ~S[1], ~S[2]);  // And

  // Other names for the same wires on the sheet: sAC[2:0] = S
endmodule
