// Digital circuit CPU.dig as structural Verilog
module CPU (
  input  CLK,
  output [7:0] AC,
  output neg,
  output Over,
  output [7:0] MQ,
  output [7:0] N,
  output [2:0] OpCode
);

  wire button_1_out, IR, MAROperando, \MAROperação , PC, PC_ovf;
  wire [2:0] S;
  wire [7:0] AC_t, BUS, MAROperandos_q, \MAROperações_q , Mem, MQ_t, PC_out;

  Register #(.Bits(8)) MAROperandos (.D(Mem), .C(CLK), .en(1'b1), .Q(MAROperandos_q));
  EEPROMDualPort #(.AddrBits(8), .Bits(8)) Operandos (.A(BUS), .Din({8{1'b0}}), .str(1'b0), .C(CLK), .ld(1'b1), .D(N));
  Button button_1 (.out(button_1_out));
  Counter #(.Bits(8)) u_PC (.en(PC), .C(CLK), .clr(1'b0), .out(PC_out), .ovf(PC_ovf));
  Register #(.Bits(3)) u_IR (.D(OpCode), .C(CLK), .en(1'b1), .Q(S));
  ControlUnit CC (
    .CLK(CLK), .bt(button_1_out), .PC(PC), .\MAROperação (\MAROperação ), .MAROperando(MAROperando), .IR(IR));
  assign BUS[0] = MAROperando ? MAROperandos_q[0] : 1'bz;  // Driver driver_1
  assign Mem[0] = PC ? PC_out[0] : 1'bz;  // Driver driver_2
  Register #(.Bits(8)) \MAROperações  (.D(Mem), .C(CLK), .en(1'b1), .Q(\MAROperações_q ));
  EEPROMDualPort #(.AddrBits(8), .Bits(3)) \Operações  (
    .A(BUS), .Din(3'b000), .str(1'b0), .C(CLK), .ld(1'b1), .D(OpCode));
  assign BUS[0] = \MAROperação  ? \MAROperações_q [0] : 1'bz;  // Driver driver_3
  Register #(.Bits(8)) u_AC (.D(AC_t), .C(CLK), .en(1'b1), .Q(AC));
  ALU8bits ALU (.N(N), .S(S), .CLK(CLK), .MQ(MQ_t), .neg(neg), .AC(AC_t), .Over(Over));
  Register #(.Bits(8)) u_MQ (.D(MQ_t), .C(CLK), .en(1'b1), .Q(MQ));
  // Pins of 1 and 8 bits meet at Mem
  // Pins of 1 and 8 bits meet at MAROperandos_q
  // Pins of 1 and 8 bits meet at \MAROperações_q 
  // Pins of 1 and 8 bits meet at BUS
  // Pins of 1 and 8 bits meet at PC_out
  // also tied to GND on the sheet: PC_ovf

  // Other names for the same wires on the sheet: IROp[2:0] = OpCode

  // Notes on the sheet:
  //   contents of Operandos (hex, n*v repeats v):
  //   1,2,3,4,5,6
endmodule
