// Digital circuit CPUHarvard.dig as structural Verilog
module CPUHarvard (
  input  Enable,
  input  CLK,
  output [7:0] MQ,
  output Neg,
  output [7:0] AC,
  output Over
);

  wire [2:0] S;
  wire [7:0] N, OUT;
  wire [11:11] rom_1_d;

  Counter #(.Bits(8)) counter_1 (.en(Enable), .C(CLK), .clr(1'b0), .out(OUT));  // open: ovf
  ROM #(.AddrBits(8), .Bits(12)) rom_1 (.A(OUT), .sel(1'b1), .D({rom_1_d[11], N, S}));
  ALU8bits alu8bits_1 (.N(N), .S(S), .CLK(CLK), .MQ(MQ), .neg(Neg), .AC(AC), .Over(Over));

  // Other names for the same wires on the sheet: EN = Enable

  // Notes on the sheet:
  //   contents of rom_1 (hex, n*v repeats v):
  //   28
endmodule
