// Digital circuit ControlUnit.dig as structural Verilog
module ControlUnit (
  input  CLK,
  input  bt,
  output PC,
  output \MAROperação ,
  output MAROperando,
  output IR
);

  wire Q1, Q3;

  RingCounter8bits ringcounter8bits_1 (
    .clk(CLK), .bt(bt), .Q0(\MAROperação ), .Q1(Q1), .Q2(MAROperando), .Q3(Q3), .Q4(PC));
  xor xor_1 (IR, Q1, Q3);

  // Other names for the same wires on the sheet: Q0 = \MAROperação ; Q2 = MAROperando; Q4 = PC
endmodule
