// Digital circuit LeftShift8bits.dig as structural Verilog
module LeftShift8bits (
  input  [7:0] A,
  output [7:0] ALS
);

  // Pins of 1 and 8 bits meet at {A[6:0], 1'b0}

  assign ALS = {A[6:0], 1'b0};
endmodule
