// Digital circuit RightShift8bits.dig as structural Verilog
module RightShift8bits (
  input  [7:0] A,
  output [7:0] ARS
);

  // Pins of 1 and 8 bits meet at {1'b0, A[7:1]}

  assign ARS = {1'b0, A[7:1]};
endmodule
