// Digital circuit divisor8bits.dig as structural Verilog
module divisor8bits (
  input  [7:0] A,
  input  [7:0] B,
  output [7:0] R,
  output [7:0] Q
);

  wire PU0_2_r, PU0_3_r, PU0_4_r, PU0_5_r, PU0_6_r, PU0_7_r, PU0_r, PU1_2_cout, PU1_3_cout, PU1_4_cout,
       PU1_5_cout, PU1_6_cout, PU1_7_cout, PU1_cout, PU2_2_cout, PU2_3_cout, PU2_4_cout, PU2_5_cout,
       PU2_6_cout, PU2_7_cout, PU2_cout, PU3_2_cout, PU3_3_cout, PU3_4_cout, PU3_5_cout, PU3_6_cout,
       PU3_7_cout, PU3_cout, PU4_2_cout, PU4_3_cout, PU4_4_cout, PU4_5_cout, PU4_6_cout, PU4_7_cout,
       PU4_cout, PU5_2_cout, PU5_3_cout, PU5_4_cout, PU5_5_cout, PU5_6_cout, PU5_7_cout, PU5_cout,
       PU6_2_cout, PU6_3_cout, PU6_4_cout, PU6_5_cout, PU6_6_cout, PU6_cout, PU7_2_cout, PU7_3_cout,
       PU7_4_cout, PU7_5_cout, PU7_6_cout, PU7_7_cout, PU7_8_cout, PU7_cout, PU9_cout, PU10_cout, PU11_cout,
       PU12_cout, PU13_cout, PU14_cout, PU15_cout, r0_t, r1_t, r2_t, r3_t, r4_t, r5_t, r6_t, r7_t, r8, r9,
       r10, r11, r12, r13, r14, r15, r16, r17, r18, r19, r20, r21, r22, r23, r24, r25, r26, r27, r28, r29,
       r30, r31, r32, r33, r34, r35, r36, r37, r38, r39, r40, r41, r42, r43, r44, r45, r46, r47, r48;

  subRestore1bit PU0 (.A(1'b0), .B(B[7]), .Cin(PU1_cout), .S(Q[7]), .R(PU0_r), .Cout(Q[7]));
  subRestore1bit PU1 (.A(1'b0), .B(B[6]), .Cin(PU2_cout), .S(Q[7]), .R(r6_t), .Cout(PU1_cout));
  subRestore1bit PU0_2 (.A(r6_t), .B(B[7]), .Cin(PU1_2_cout), .S(Q[6]), .R(PU0_2_r), .Cout(Q[6]));
  subRestore1bit PU2 (.A(1'b0), .B(B[5]), .Cin(PU3_cout), .S(Q[7]), .R(r5_t), .Cout(PU2_cout));
  subRestore1bit PU1_2 (.A(r5_t), .B(B[6]), .Cin(PU2_2_cout), .S(Q[6]), .R(r13), .Cout(PU1_2_cout));
  subRestore1bit PU0_3 (.A(r13), .B(B[7]), .Cin(PU1_3_cout), .S(Q[5]), .R(PU0_3_r), .Cout(Q[5]));
  subRestore1bit PU3 (.A(1'b0), .B(B[4]), .Cin(PU4_cout), .S(Q[7]), .R(r4_t), .Cout(PU3_cout));
  subRestore1bit PU2_2 (.A(r4_t), .B(B[5]), .Cin(PU3_2_cout), .S(Q[6]), .R(r12), .Cout(PU2_2_cout));
  subRestore1bit PU1_3 (.A(r12), .B(B[6]), .Cin(PU2_3_cout), .S(Q[5]), .R(r20), .Cout(PU1_3_cout));
  subRestore1bit PU0_4 (.A(r20), .B(B[7]), .Cin(PU1_4_cout), .S(Q[4]), .R(PU0_4_r), .Cout(Q[4]));
  subRestore1bit PU4 (.A(1'b0), .B(B[3]), .Cin(PU5_cout), .S(Q[7]), .R(r3_t), .Cout(PU4_cout));
  subRestore1bit PU3_2 (.A(r3_t), .B(B[4]), .Cin(PU4_2_cout), .S(Q[6]), .R(r11), .Cout(PU3_2_cout));
  subRestore1bit PU2_3 (.A(r11), .B(B[5]), .Cin(PU3_3_cout), .S(Q[5]), .R(r19), .Cout(PU2_3_cout));
  subRestore1bit PU1_4 (.A(r19), .B(B[6]), .Cin(PU2_4_cout), .S(Q[4]), .R(r27), .Cout(PU1_4_cout));
  subRestore1bit PU0_5 (.A(r27), .B(B[7]), .Cin(PU1_5_cout), .S(Q[3]), .R(PU0_5_r), .Cout(Q[3]));
  subRestore1bit PU5 (.A(1'b0), .B(B[2]), .Cin(PU6_cout), .S(Q[7]), .R(r2_t), .Cout(PU5_cout));
  subRestore1bit PU4_2 (.A(r2_t), .B(B[3]), .Cin(PU5_2_cout), .S(Q[6]), .R(r10), .Cout(PU4_2_cout));
  subRestore1bit PU3_3 (.A(r10), .B(B[4]), .Cin(PU4_3_cout), .S(Q[5]), .R(r18), .Cout(PU3_3_cout));
  subRestore1bit PU2_4 (.A(r18), .B(B[5]), .Cin(PU3_4_cout), .S(Q[4]), .R(r26), .Cout(PU2_4_cout));
  subRestore1bit PU1_5 (.A(r26), .B(B[6]), .Cin(PU2_5_cout), .S(Q[3]), .R(r34), .Cout(PU1_5_cout));
  subRestore1bit PU0_6 (.A(r34), .B(B[7]), .Cin(PU1_6_cout), .S(Q[2]), .R(PU0_6_r), .Cout(Q[2]));
  subRestore1bit PU6 (.A(1'b0), .B(B[1]), .Cin(PU7_cout), .S(Q[7]), .R(r1_t), .Cout(PU6_cout));
  subRestore1bit PU5_2 (.A(r1_t), .B(B[2]), .Cin(PU6_2_cout), .S(Q[6]), .R(r9), .Cout(PU5_2_cout));
  subRestore1bit PU4_3 (.A(r9), .B(B[3]), .Cin(PU5_3_cout), .S(Q[5]), .R(r17), .Cout(PU4_3_cout));
  subRestore1bit PU3_4 (.A(r17), .B(B[4]), .Cin(PU4_4_cout), .S(Q[4]), .R(r25), .Cout(PU3_4_cout));
  subRestore1bit PU2_5 (.A(r25), .B(B[5]), .Cin(PU3_5_cout), .S(Q[3]), .R(r33), .Cout(PU2_5_cout));
  subRestore1bit PU1_6 (.A(r33), .B(B[6]), .Cin(PU2_6_cout), .S(Q[2]), .R(r41), .Cout(PU1_6_cout));
  subRestore1bit PU0_7 (.A(r41), .B(B[7]), .Cin(PU1_7_cout), .S(Q[1]), .R(PU0_7_r), .Cout(Q[1]));
  subRestore1bit PU7 (.A(A[7]), .B(B[0]), .Cin(1'b1), .S(Q[7]), .R(r0_t), .Cout(PU7_cout));
  subRestore1bit PU6_2 (.A(r0_t), .B(B[1]), .Cin(PU7_2_cout), .S(Q[6]), .R(r8), .Cout(PU6_2_cout));
  subRestore1bit PU5_3 (.A(r8), .B(B[2]), .Cin(PU6_3_cout), .S(Q[5]), .R(r16), .Cout(PU5_3_cout));
  subRestore1bit PU4_4 (.A(r16), .B(B[3]), .Cin(PU5_4_cout), .S(Q[4]), .R(r24), .Cout(PU4_4_cout));
  subRestore1bit PU3_5 (.A(r24), .B(B[4]), .Cin(PU4_5_cout), .S(Q[3]), .R(r32), .Cout(PU3_5_cout));
  subRestore1bit PU2_6 (.A(r32), .B(B[5]), .Cin(PU3_6_cout), .S(Q[2]), .R(r40), .Cout(PU2_6_cout));
  subRestore1bit PU1_7 (.A(r40), .B(B[6]), .Cin(PU2_7_cout), .S(Q[1]), .R(r48), .Cout(PU1_7_cout));
  subRestore1bit PU8 (.A(r48), .B(B[7]), .Cin(PU9_cout), .S(Q[0]), .R(R[7]), .Cout(Q[0]));
  subRestore1bit PU7_2 (.A(A[6]), .B(B[0]), .Cin(1'b1), .S(Q[6]), .R(r7_t), .Cout(PU7_2_cout));
  subRestore1bit PU6_3 (.A(r7_t), .B(B[1]), .Cin(PU7_3_cout), .S(Q[5]), .R(r15), .Cout(PU6_3_cout));
  subRestore1bit PU5_4 (.A(r15), .B(B[2]), .Cin(PU7_4_cout), .S(Q[4]), .R(r23), .Cout(PU5_4_cout));
  subRestore1bit PU4_5 (.A(r23), .B(B[3]), .Cin(PU5_5_cout), .S(Q[3]), .R(r31), .Cout(PU4_5_cout));
  subRestore1bit PU3_6 (.A(r31), .B(B[4]), .Cin(PU4_6_cout), .S(Q[2]), .R(r39), .Cout(PU3_6_cout));
  subRestore1bit PU2_7 (.A(r39), .B(B[5]), .Cin(PU3_7_cout), .S(Q[1]), .R(r47), .Cout(PU2_7_cout));
  subRestore1bit PU9 (.A(r47), .B(B[6]), .Cin(PU10_cout), .S(Q[0]), .R(R[6]), .Cout(PU9_cout));
  subRestore1bit PU7_3 (.A(A[5]), .B(B[0]), .Cin(1'b1), .S(Q[5]), .R(r14), .Cout(PU7_3_cout));
  subRestore1bit PU7_4 (.A(r14), .B(B[1]), .Cin(PU7_5_cout), .S(Q[4]), .R(r22), .Cout(PU7_4_cout));
  subRestore1bit PU5_5 (.A(r22), .B(B[2]), .Cin(PU6_4_cout), .S(Q[3]), .R(r30), .Cout(PU5_5_cout));
  subRestore1bit PU4_6 (.A(r30), .B(B[3]), .Cin(PU5_6_cout), .S(Q[2]), .R(r38), .Cout(PU4_6_cout));
  subRestore1bit PU3_7 (.A(r38), .B(B[4]), .Cin(PU4_7_cout), .S(Q[1]), .R(r46), .Cout(PU3_7_cout));
  subRestore1bit PU10 (.A(r46), .B(B[5]), .Cin(PU11_cout), .S(Q[0]), .R(R[5]), .Cout(PU10_cout));
  subRestore1bit PU7_5 (.A(A[4]), .B(B[0]), .Cin(1'b1), .S(Q[4]), .R(r21), .Cout(PU7_5_cout));
  subRestore1bit PU6_4 (.A(r21), .B(B[1]), .Cin(PU7_6_cout), .S(Q[3]), .R(r29), .Cout(PU6_4_cout));
  subRestore1bit PU5_6 (.A(r29), .B(B[2]), .Cin(PU6_5_cout), .S(Q[2]), .R(r37), .Cout(PU5_6_cout));
  subRestore1bit PU4_7 (.A(r37), .B(B[3]), .Cin(PU5_7_cout), .S(Q[1]), .R(r45), .Cout(PU4_7_cout));
  subRestore1bit PU11 (.A(r45), .B(B[4]), .Cin(PU12_cout), .S(Q[0]), .R(R[4]), .Cout(PU11_cout));
  subRestore1bit PU7_6 (.A(A[3]), .B(B[0]), .Cin(1'b1), .S(Q[3]), .R(r28), .Cout(PU7_6_cout));
  subRestore1bit PU6_5 (.A(r28), .B(B[1]), .Cin(PU7_7_cout), .S(Q[2]), .R(r36), .Cout(PU6_5_cout));
  subRestore1bit PU5_7 (.A(r36), .B(B[2]), .Cin(PU6_6_cout), .S(Q[1]), .R(r44), .Cout(PU5_7_cout));
  subRestore1bit PU12 (.A(r44), .B(B[3]), .Cin(PU13_cout), .S(Q[0]), .R(R[3]), .Cout(PU12_cout));
  subRestore1bit PU7_7 (.A(A[2]), .B(B[0]), .Cin(1'b1), .S(Q[2]), .R(r35), .Cout(PU7_7_cout));
  subRestore1bit PU6_6 (.A(r35), .B(B[1]), .Cin(PU7_8_cout), .S(Q[1]), .R(r43), .Cout(PU6_6_cout));
  subRestore1bit PU13 (.A(r43), .B(B[2]), .Cin(PU14_cout), .S(Q[0]), .R(R[2]), .Cout(PU13_cout));
  subRestore1bit PU7_8 (.A(A[1]), .B(B[0]), .Cin(1'b1), .S(Q[1]), .R(r42), .Cout(PU7_8_cout));
  subRestore1bit PU14 (.A(r42), .B(B[1]), .Cin(PU15_cout), .S(Q[0]), .R(R[1]), .Cout(PU14_cout));
  subRestore1bit PU15 (.A(A[0]), .B(B[0]), .Cin(1'b1), .S(Q[0]), .R(R[0]), .Cout(PU15_cout));
  // also tied to GND on the sheet: {PU0_2_r, PU0_3_r, PU0_4_r, PU0_5_r, PU0_6_r, PU0_7_r, PU0_r}

  // Other names for the same wires on the sheet: D0 = A[0]; D1 = A[1]; D2 = A[2]; D3 = A[3]; D4 = A[4]; D5 = A[5];
  //   D6 = A[6]; D7 = A[7]; d0_t = B[0]; d1_t = B[1]; d2_t = B[2]; d3_t = B[3]; d4_t = B[4]; d5_t = B[5]; d6_t = B[6];
  //   d7_t = B[7]; Cout7 = Q[0]; Cout6 = Q[1]; Cout5 = Q[2]; Cout4 = Q[3]; Cout3 = Q[4]; Cout2 = Q[5]; Cout1 = Q[6];
  //   Cout0 = Q[7]
endmodule
