// Digital circuit inversor8bits.dig as structural Verilog
module inversor8bits (
  input  [7:0] A,
  output Ainv
);

  wire [7:0] not_1_out;

  assign not_1_out = ~A;  // Not not_1, 8 bits wide
  soma8bits soma8bits_1 (.A(not_1_out), .B(8'h1), .S(Ainv));  // open: Over
endmodule
