// Digital circuit multiplicacao8bits.dig as structural Verilog
module multiplicacao8bits (
  input  [7:0] A,
  input  [7:0] B,
  output [7:0] LSB,
  output [7:0] MSB
);

  wire Cout0, Cout1, Cout2, Cout3, Cout4, Cout5, Cout6, Cout7, Cout8, Cout9, Cout10, Cout11, Cout12, Cout13,
       Cout14, Cout15, Cout16, Cout17, Cout18, Cout19, Cout20, Cout21, Cout22, Cout23, Cout24, Cout25,
       Cout26, Cout27, Cout28, Cout29, Cout30, Cout31, Cout32, Cout33, Cout34, Cout35, Cout36, Cout37,
       Cout38, Cout39, Cout40, Cout41, Cout42, Cout43, Cout44, Cout45, Cout46, Cout47, Cout48, Cout49,
       Cout50, Cout51, Cout52, Cout53, Cout54, PP0, PP1, PP2, PP3, PP4, PP5, PP6, PP7, PP8, PP9, PP10, PP11,
       PP12, PP13, PP14, PP15, PP16, PP17, PP18, PP19, PP20, PP21, PP22, PP23, PP24, PP25, PP26, PP27, PP28,
       PP29, PP30, PP31, PP32, PP33, PP34, PP35, PP36, PP37, PP38, PP39, PP40, PP41, PP43, PP44, PP45, PP46,
       PP47, PP48, PP49, PP50, PP51, PP52, PP53, PP54, PP55, PP56, PP57, PP58, PP59, PP60, PP61, PP62, PP63,
       SP0, SP1, SP2, SP3, SP4, SP5, SP6, SP7, SP8, SP9, SP10, SP11, SP12, SP13, SP14, SP15, SP16, SP17,
       SP18, SP19, SP20, SP21, SP22, SP23, SP24, SP25, SP26, SP27, SP28, SP29, SP30, SP31, SP32, SP33, SP34,
       SP35, SP36, SP37, SP38, SP39, SP40, SP41;

  and and_1 (PP63, B[7], A[7]);
  and and_2 (PP61, B[6], A[7]);
  and and_3 (PP62, B[7], A[6]);
  and and_4 (PP58, B[5], A[7]);
  and and_5 (PP59, B[6], A[6]);
  and and_6 (PP60, B[7], A[5]);
  and and_7 (PP54, B[4], A[7]);
  and and_8 (PP55, B[5], A[6]);
  and and_9 (PP56, B[6], A[5]);
  and and_10 (PP57, B[7], A[4]);
  and and_11 (PP49, B[3], A[7]);
  and and_12 (PP50, B[4], A[6]);
  and and_13 (PP51, B[5], A[5]);
  and and_14 (PP52, B[6], A[4]);
  and and_15 (PP53, B[7], A[3]);
  and and_16 (PP43, B[2], A[7]);
  and and_17 (PP44, B[3], A[6]);
  and and_18 (PP45, B[4], A[5]);
  and and_19 (PP46, B[5], A[4]);
  and and_20 (PP47, B[6], A[3]);
  and and_21 (PP48, B[7], A[2]);
  and and_22 (PP35, B[1], A[7]);
  and and_23 (PP36, B[2], A[6]);
  and and_24 (PP37, B[3], A[5]);
  and and_25 (PP38, B[4], A[4]);
  and and_26 (PP39, B[5], A[3]);
  and and_27 (PP40, B[6], A[2]);
  and and_28 (PP41, B[7], A[1]);
  and and_29 (PP27, B[0], A[7]);
  and and_30 (PP28, B[1], A[6]);
  and and_31 (PP29, B[2], A[5]);
  and and_32 (PP30, B[3], A[4]);
  and and_33 (PP31, B[4], A[3]);
  and and_34 (PP32, B[5], A[2]);
  and and_35 (PP33, B[6], A[1]);
  and and_36 (PP34, B[7], A[0]);
  and and_37 (PP20, B[0], A[6]);
  and and_38 (PP21, B[1], A[5]);
  and and_39 (PP22, B[2], A[4]);
  and and_40 (PP23, B[3], A[3]);
  and and_41 (PP24, B[4], A[2]);
  and and_42 (PP25, B[5], A[1]);
  and and_43 (PP26, B[6], A[0]);
  and and_44 (PP14, B[0], A[5]);
  and and_45 (PP15, B[1], A[4]);
  and and_46 (PP16, B[2], A[3]);
  and and_47 (PP17, B[3], A[2]);
  and and_48 (PP18, B[4], A[1]);
  and and_49 (PP19, B[5], A[0]);
  and and_50 (PP9, B[0], A[4]);
  and and_51 (PP10, B[1], A[3]);
  and and_52 (PP11, B[2], A[2]);
  and and_53 (PP12, B[3], A[1]);
  and and_54 (PP13, B[4], A[0]);
  and and_55 (PP5, B[0], A[3]);
  and and_56 (PP6, B[1], A[2]);
  and and_57 (PP7, B[2], A[1]);
  and and_58 (PP8, B[3], A[0]);
  and and_59 (PP2, B[0], A[2]);
  and and_60 (PP3, B[1], A[1]);
  and and_61 (PP4, B[2], A[0]);
  and and_62 (PP0, B[0], A[1]);
  and and_63 (PP1, B[1], A[0]);
  and and_64 (LSB[0], B[0], A[0]);
  soma1bit PP0_plus_PP1 (.A(PP0), .B(PP1), .Cin(1'b0), .S(LSB[1]), .Cout(Cout0));
  soma1bit PP2_plus_PP3 (.A(PP2), .B(PP3), .Cin(Cout0), .S(SP0), .Cout(Cout1));
  soma1bit PP5_plus_PP6 (.A(PP5), .B(PP6), .Cin(Cout1), .S(SP1), .Cout(Cout3));
  soma1bit PP9_plus_PP10 (.A(PP9), .B(PP10), .Cin(Cout3), .S(SP3), .Cout(Cout6));
  soma1bit PP14_plus_PP15 (.A(PP14), .B(PP15), .Cin(Cout6), .S(SP6), .Cout(Cout10));
  soma1bit PP20_plus_PP21 (.A(PP20), .B(PP21), .Cin(Cout10), .S(SP10), .Cout(Cout15));
  soma1bit PP27_plus_PP28 (.A(PP27), .B(PP28), .Cin(Cout15), .S(SP15), .Cout(Cout21));
  soma1bit soma1bit_1 (.A(PP35), .B(Cout21), .Cin(1'b0), .S(SP21), .Cout(Cout28));
  soma1bit SP0_plus_PP4 (.A(SP0), .B(PP4), .Cin(1'b0), .S(LSB[2]), .Cout(Cout2));
  soma1bit SP1_plus_PP7 (.A(SP1), .B(PP7), .Cin(Cout2), .S(SP2), .Cout(Cout4));
  soma1bit SP3_plus_PP11 (.A(SP3), .B(PP11), .Cin(Cout4), .S(SP4), .Cout(Cout7));
  soma1bit SP6_plus_PP16 (.A(SP6), .B(PP16), .Cin(Cout7), .S(SP7), .Cout(Cout11));
  soma1bit SP10_plus_PP22 (.A(SP10), .B(PP22), .Cin(Cout11), .S(SP11), .Cout(Cout16));
  soma1bit SP15_plus_PP29 (.A(SP15), .B(PP29), .Cin(Cout16), .S(SP16), .Cout(Cout22));
  soma1bit soma1bit_2 (.A(SP21), .B(PP36), .Cin(Cout22), .S(SP22), .Cout(Cout29));
  soma1bit soma1bit_3 (.A(PP43), .B(Cout28), .Cin(Cout29), .S(SP27), .Cout(Cout35));
  soma1bit SP2_plus_PP8 (.A(SP2), .B(PP8), .Cin(1'b0), .S(LSB[3]), .Cout(Cout5));
  soma1bit SP4_plus_PP12 (.A(SP4), .B(PP12), .Cin(Cout5), .S(SP5), .Cout(Cout8));
  soma1bit SP7_plus_PP17 (.A(SP7), .B(PP17), .Cin(Cout8), .S(SP8), .Cout(Cout12));
  soma1bit SP11_plus_PP23 (.A(SP11), .B(PP23), .Cin(Cout12), .S(SP12), .Cout(Cout17));
  soma1bit SP16_plus_PP30 (.A(SP16), .B(PP30), .Cin(Cout17), .S(SP17), .Cout(Cout23));
  soma1bit soma1bit_4 (.A(SP22), .B(PP37), .Cin(Cout23), .S(SP23), .Cout(Cout30));
  soma1bit soma1bit_5 (.A(SP27), .B(PP44), .Cin(Cout30), .S(SP28), .Cout(Cout36));
  soma1bit soma1bit_6 (.A(PP49), .B(Cout35), .Cin(Cout36), .S(SP32), .Cout(Cout41));
  soma1bit SP5_plus_PP13 (.A(SP5), .B(PP13), .Cin(1'b0), .S(LSB[4]), .Cout(Cout9));
  soma1bit SP8_plus_PP18 (.A(SP8), .B(PP18), .Cin(Cout9), .S(SP9), .Cout(Cout13));
  soma1bit SP12_plus_PP24 (.A(SP12), .B(PP24), .Cin(Cout13), .S(SP13), .Cout(Cout18));
  soma1bit SP17_plus_PP31 (.A(SP17), .B(PP31), .Cin(Cout18), .S(SP18), .Cout(Cout24));
  soma1bit soma1bit_7 (.A(SP23), .B(PP38), .Cin(Cout24), .S(SP24), .Cout(Cout31));
  soma1bit soma1bit_8 (.A(SP28), .B(PP45), .Cin(Cout31), .S(SP29), .Cout(Cout37));
  soma1bit soma1bit_9 (.A(SP32), .B(PP50), .Cin(Cout37), .S(SP33), .Cout(Cout42));
  soma1bit soma1bit_10 (.A(PP54), .B(Cout41), .Cin(Cout42), .S(SP36), .Cout(Cout46));
  soma1bit SP9_plus_PP19 (.A(SP9), .B(PP19), .Cin(1'b0), .S(LSB[5]), .Cout(Cout14));
  soma1bit SP13_plus_PP25 (.A(SP13), .B(PP25), .Cin(Cout14), .S(SP14), .Cout(Cout19));
  soma1bit SP18_plus_PP32 (.A(SP18), .B(PP32), .Cin(Cout19), .S(SP19), .Cout(Cout25));
  soma1bit soma1bit_11 (.A(SP24), .B(PP39), .Cin(Cout25), .S(SP25), .Cout(Cout32));
  soma1bit soma1bit_12 (.A(SP29), .B(PP46), .Cin(Cout32), .S(SP30), .Cout(Cout38));
  soma1bit soma1bit_13 (.A(SP33), .B(PP51), .Cin(Cout38), .S(SP34), .Cout(Cout43));
  soma1bit soma1bit_14 (.A(SP36), .B(PP55), .Cin(Cout43), .S(SP37), .Cout(Cout47));
  soma1bit soma1bit_15 (.A(PP58), .B(Cout46), .Cin(Cout47), .S(SP39), .Cout(Cout50));
  soma1bit SP14_plus_PP26 (.A(SP14), .B(PP26), .Cin(1'b0), .S(LSB[6]), .Cout(Cout20));
  soma1bit SP19_plus_PP33 (.A(SP19), .B(PP33), .Cin(Cout20), .S(SP20), .Cout(Cout26));
  soma1bit soma1bit_16 (.A(SP25), .B(PP40), .Cin(Cout26), .S(SP26), .Cout(Cout33));
  soma1bit soma1bit_17 (.A(SP30), .B(PP47), .Cin(Cout33), .S(SP31), .Cout(Cout39));
  soma1bit soma1bit_18 (.A(SP34), .B(PP52), .Cin(Cout39), .S(SP35), .Cout(Cout44));
  soma1bit soma1bit_19 (.A(SP37), .B(PP56), .Cin(Cout44), .S(SP38), .Cout(Cout48));
  soma1bit soma1bit_20 (.A(SP39), .B(PP59), .Cin(Cout48), .S(SP40), .Cout(Cout51));
  soma1bit soma1bit_21 (.A(PP61), .B(Cout50), .Cin(Cout51), .S(SP41), .Cout(Cout53));
  soma1bit SP20_plus_PP34 (.A(SP20), .B(PP34), .Cin(1'b0), .S(LSB[7]), .Cout(Cout27));
  soma1bit soma1bit_22 (.A(SP26), .B(PP41), .Cin(Cout27), .S(MSB[0]), .Cout(Cout34));
  soma1bit soma1bit_23 (.A(SP31), .B(PP48), .Cin(Cout34), .S(MSB[1]), .Cout(Cout40));
  soma1bit soma1bit_24 (.A(SP35), .B(PP53), .Cin(Cout40), .S(MSB[2]), .Cout(Cout45));
  soma1bit soma1bit_25 (.A(SP38), .B(PP57), .Cin(Cout45), .S(MSB[3]), .Cout(Cout49));
  soma1bit soma1bit_26 (.A(SP40), .B(PP60), .Cin(Cout49), .S(MSB[4]), .Cout(Cout52));
  soma1bit soma1bit_27 (.A(SP41), .B(PP62), .Cin(Cout52), .S(MSB[5]), .Cout(Cout54));
  soma1bit soma1bit_28 (.A(PP63), .B(Cout53), .Cin(Cout54), .S(MSB[6]), .Cout(MSB[7]));

  // Other names for the same wires on the sheet: P0 = LSB[0]; P1 = LSB[1]; P2 = LSB[2]; P3 = LSB[3]; P4 = LSB[4];
  //   P5 = LSB[5]; P6 = LSB[6]; P7 = LSB[7]; P8 = MSB[0]; P9 = MSB[1]; P10 = MSB[2]; P11 = MSB[3]; P12 = MSB[4];
  //   P13 = MSB[5]; P14 = MSB[6]; P15 = MSB[7]
endmodule
