// Digital circuit soma.dig as structural Verilog
module soma (
  input  A1,
  input  A2,
  input  A4,
  input  A8,
  input  A16,
  input  A32,
  input  A64,
  input  A128,
  input  B1,
  input  B2,
  input  B4,
  input  B8,
  input  B16,
  input  B32,
  input  B64,
  input  B128,
  input  Cin,
  output O1,
  output O2,
  output O4,
  output O8,
  output O16,
  output O32,
  output O64,
  output O128
);

  wire add_1_c_o, add_2_c_o, add_3_c_o, add_4_c_o, add_5_c_o, add_6_c_o, add_7_c_o, undriven;

  Add add_1 (.a(A1), .b(B1), .c_i(undriven), .s(O1), .c_o(add_1_c_o));
  Add add_2 (.a(A2), .b(B2), .c_i(add_1_c_o), .s(O2), .c_o(add_2_c_o));
  Add add_3 (.a(A4), .b(B4), .c_i(add_2_c_o), .s(O4), .c_o(add_3_c_o));
  Add add_4 (.a(A8), .b(B8), .c_i(add_3_c_o), .s(O8), .c_o(add_4_c_o));
  Add add_5 (.a(A16), .b(B16), .c_i(add_4_c_o), .s(O16), .c_o(add_5_c_o));
  Add add_6 (.a(A32), .b(B32), .c_i(add_5_c_o), .s(O32), .c_o(add_6_c_o));
  Add add_7 (.a(A64), .b(B64), .c_i(add_6_c_o), .s(O64), .c_o(add_7_c_o));
  Add add_8 (.a(A128), .b(B128), .c_i(add_7_c_o), .s(O128));  // open: c_o
endmodule
