// Digital circuit soma1bit.dig as structural Verilog
module soma1bit (
  input  A,
  input  B,
  input  Cin,
  output S,
  output Cout
);

  wire and_1_out, and_2_out, and_3_out, or_1_out, xor_1_out;

  and and_1 (and_1_out, Cin, B);
  and and_2 (and_2_out, Cin, A);
  xor xor_1 (xor_1_out, A, B);
  and and_3 (and_3_out, A, B);
  or or_1 (or_1_out, and_1_out, and_2_out);
  xor xor_2 (S, xor_1_out, Cin);
  or or_2 (Cout, or_1_out, and_3_out);
endmodule
