// Digital circuit soma8bits.dig as structural Verilog
module soma8bits (
  input  [7:0] A,
  input  [7:0] B,
  output [7:0] S,
  output Over
);

  wire S0_cout, S2_cout, S4_cout, S8_cout, S16_cout, S32_cout, S64_cout;

  soma1bit S0 (.A(A[0]), .B(B[0]), .Cin(1'b0), .S(S[0]), .Cout(S0_cout));
  soma1bit S2 (.A(A[1]), .B(B[1]), .Cin(S0_cout), .S(S[1]), .Cout(S2_cout));
  soma1bit S4 (.A(A[2]), .B(B[2]), .Cin(S2_cout), .S(S[2]), .Cout(S4_cout));
  soma1bit S8 (.A(A[3]), .B(B[3]), .Cin(S4_cout), .S(S[3]), .Cout(S8_cout));
  soma1bit S16 (.A(A[4]), .B(B[4]), .Cin(S8_cout), .S(S[4]), .Cout(S16_cout));
  soma1bit S32 (.A(A[5]), .B(B[5]), .Cin(S16_cout), .S(S[5]), .Cout(S32_cout));
  soma1bit S64 (.A(A[6]), .B(B[6]), .Cin(S32_cout), .S(S[6]), .Cout(S64_cout));
  soma1bit S128 (.A(A[7]), .B(B[7]), .Cin(S64_cout), .S(S[7]), .Cout(Over));
  // Pins of 1 and 8 bits meet at S

  // Other names for the same wires on the sheet: A2 = A[1]; A4 = A[2]; A8 = A[3]; A16 = A[4]; A32 = A[5]; A64 = A[6];
  //   A128 = A[7]; B2 = B[1]; B4 = B[2]; B8 = B[3]; B16 = B[4]; B32 = B[5]; B64 = B[6]; B128 = B[7]; S2 = S[1];
  //   S4 = S[2]; S8 = S[3]; S16 = S[4]; S32 = S[5]; S64 = S[6]; S128 = S[7]
endmodule
