// Digital circuit sub8bits.dig as structural Verilog
module sub8bits (
  input  [7:0] A,
  input  [7:0] B,
  output [7:0] Sub,
  output neg
);

  wire inversor8bits_1_p2;
  wire [6:0] soma8bits_1_p3;
  wire [7:0] inversor8bits_2_p2;

  // inversor8bits inversor8bits_1: pin names not known; wires that end beside it: B, inversor8bits_1_p2
  // soma8bits soma8bits_1: pin names not known; wires that end beside it: A, inversor8bits_1_p2, {neg, soma8bits_1_p3}
  // inversor8bits inversor8bits_2: pin names not known; wires that end beside it: {neg, soma8bits_1_p3}, inversor8bits_2_p2
  Multiplexer #(.Bits(8)) multiplexer_1 (.sel(neg), .in_0({neg, soma8bits_1_p3}), .in_1(inversor8bits_2_p2), .out(Sub));
endmodule
