// Digital circuit subRestore1bit.dig as structural Verilog
module subRestore1bit (
  input  A,
  input  B,
  input  Cin,
  input  S,
  output R,
  output Cout
);

  wire tBnot, tSub;

  not not_1 (tBnot, B);
  soma1bit FA (.A(A), .B(tBnot), .Cin(Cin), .S(tSub), .Cout(Cout));
  Multiplexer multiplexer_1 (.sel(S), .in_0(A), .in_1(tSub), .out(R));

  // Other names for the same wires on the sheet: tA = A; tCin = Cin; tCout = Cout
endmodule
