// Digital circuit subWRestore8bits.dig as structural Verilog
module subWRestore8bits (
  input  [7:0] A,
  input  [7:0] B,
  output [7:0] Sub
);

  wire sub8bits_1_neg;
  wire [7:0] sub8bits_1_sub;

  sub8bits sub8bits_1 (.A(A), .B(B), .Sub(sub8bits_1_sub), .neg(sub8bits_1_neg));
  Multiplexer #(.Bits(8)) multiplexer_1 (.sel(sub8bits_1_neg), .in_0(A), .in_1(sub8bits_1_sub), .out(Sub));
  // Pins of 1 and 8 bits meet at Sub
endmodule
